# Fritzing sketch BUTTON (saved by Fritzing 0.9.10b)

parts:
  M1 = >Wemos D1 R32
  S1 = Pushbutton [package="[THT]"]
  S2 = Pushbutton [package="[THT]"]

nets:
  N1: M1.GND, S1.Pin_3, S1.Pin_4, S2.Pin_3
  N2: M1.IO25, S1.Pin_1, S1.Pin_2
  N3: M1.IO27, S2.Pin_1, S2.Pin_2

custom parts:
  >Wemos D1 R32: Wemos D1 R32 - This board is used with dual-mode Wi-Fi and Bluetooth chips, which is safe, reliable, and scalable to a variety of applications. DC in 5V-12V, 1 analog input(3.2V max input), a Micro USB connection, Compatible with D1 R32=WiFi+bluetooth+UNO
