# Fritzing sketch DHT22 (saved by Fritzing 0.9.10b)
breadboards: 1

parts:
  M1 = >Wemos D1 R32
  RHT1 = Humidity and Temperature Sensor RHT03

nets:
  5V: M1.5V, RHT1.Vcc
  N1: M1.GND, RHT1.GND_2
  N2: M1.IO16, RHT1.Data-signal

custom parts:
  >Wemos D1 R32: Wemos D1 R32 - This board is used with dual-mode Wi-Fi and Bluetooth chips, which is safe, reliable, and scalable to a variety of applications. DC in 5V-12V, 1 analog input(3.2V max input), a Micro USB connection, Compatible with D1 R32=WiFi+bluetooth+UNO
