# Fritzing sketch DISPLAY TFT (saved by Fritzing 0.9.10b)

parts:
  M1 = >Wemos D1 R32
  Componente1 = TFT 2.2 inch 320x240 w microSD [part_number=1480]

nets:
  5V: M1.5V, Componente1.VIN
  N1: M1.3V3, Componente1.BACKLIGHT
  GND: M1.GND, Componente1.GND
  N2: M1.IO2, Componente1.DC
  N3: M1.IO4, Componente1.RESET
  N4: M1.IO12, Componente1.LCDCS
  N5: M1.IO23, Componente1.MOSI
  N6: M1.IO19, Componente1.MISO
  N7: M1.IO18, Componente1.SCLK

custom parts:
  >Wemos D1 R32: Wemos D1 R32 - This board is used with dual-mode Wi-Fi and Bluetooth chips, which is safe, reliable, and scalable to a variety of applications. DC in 5V-12V, 1 analog input(3.2V max input), a Micro USB connection, Compatible with D1 R32=WiFi+bluetooth+UNO
  TFT 2.2 inch 320x240 w microSD: This lovely little display breakout is the best way to add a small, colorful and bright display to any project. Since the display uses 4-wire SPI to communicate and has its own pixel-addressable frame buffer, it can be used with every kind of microcontroller. Even a very small one with low memory and few pins available! The 2.2" display has 320x240 color pixels.
