# Fritzing sketch GEIGER COUNTER (saved by Fritzing 0.9.10b)

parts:
  M1 = >Wemos D1 R32
  J1 = Dagu DGServo 9g header (male) [package=THT]

nets:
  5V: M1.5V, J1.Vcc
  GND: M1.GND, J1.gnd
  N1: M1.IO39, J1.pulse

custom parts:
  >Wemos D1 R32: Wemos D1 R32 - This board is used with dual-mode Wi-Fi and Bluetooth chips, which is safe, reliable, and scalable to a variety of applications. DC in 5V-12V, 1 analog input(3.2V max input), a Micro USB connection, Compatible with D1 R32=WiFi+bluetooth+UNO
