# Fritzing sketch LED (saved by Fritzing 0.9.10b)

parts:
  LED1 = LEDs [package=led10mm]
  M1 = >Wemos D1 R32
  R1 = Resistor [tolerance=±5% power=0.25 resistance=220 package=THT]  # not connected

nets:
  N1: LED1.C, M1.IO17

custom parts:
  >Wemos D1 R32: Wemos D1 R32 - This board is used with dual-mode Wi-Fi and Bluetooth chips, which is safe, reliable, and scalable to a variety of applications. DC in 5V-12V, 1 analog input(3.2V max input), a Micro USB connection, Compatible with D1 R32=WiFi+bluetooth+UNO
