# Fritzing sketch POTENTIOMETER (saved by Fritzing 0.9.10b)

parts:
  U1 = POT [knob_status=50% power=0.5W package=pot_mammoth]
  M1 = >Wemos D1 R32

nets:
  N1: U1.S, M1.5V
  N2: U1.A, M1.IO34
  N3: U1.E, M1.GND

custom parts:
  >Wemos D1 R32: Wemos D1 R32 - This board is used with dual-mode Wi-Fi and Bluetooth chips, which is safe, reliable, and scalable to a variety of applications. DC in 5V-12V, 1 analog input(3.2V max input), a Micro USB connection, Compatible with D1 R32=WiFi+bluetooth+UNO
