# Fritzing sketch RADIO FM (saved by Fritzing 0.9.10b)

parts:
  M1 = TEA5767 [package=THT]
  M2 = >Wemos D1 R32

nets:
  N1: M1.pin1, M2.5V
  N2: M1.pin2, M2.SDA
  N3: M1.pin3, M2.SCL
  N4: M1.pin4, M2.GND

custom parts:
  TEA5767: SMAKN brand new 76-108MHZ 5V TEA5767 FM Stereo Radio Module with Cable Antenna for Arduino EK1705(New version)
  >Wemos D1 R32: Wemos D1 R32 - This board is used with dual-mode Wi-Fi and Bluetooth chips, which is safe, reliable, and scalable to a variety of applications. DC in 5V-12V, 1 analog input(3.2V max input), a Micro USB connection, Compatible with D1 R32=WiFi+bluetooth+UNO
