# Fritzing sketch SD CARD MODULE (saved by Fritzing 0.9.10b)

parts:
  M1 = >Wemos D1 R32
  SD_card_module1 = SD Card Module

nets:
  N1: M1.5V, SD_card_module1.+5
  GND: M1.GND, SD_card_module1.GND
  N2: M1.IO5, SD_card_module1.CS
  N3: M1.IO23, SD_card_module1.MOSI
  N4: M1.IO19, SD_card_module1.MISO
  N5: M1.IO18, SD_card_module1.SCK

custom parts:
  >Wemos D1 R32: Wemos D1 R32 - This board is used with dual-mode Wi-Fi and Bluetooth chips, which is safe, reliable, and scalable to a variety of applications. DC in 5V-12V, 1 analog input(3.2V max input), a Micro USB connection, Compatible with D1 R32=WiFi+bluetooth+UNO
  SD Card Module: SD Card Module Slot Socket Reader For Arduino ARM MCU
